// Logisim project complement_a_2.circ as structural Verilog
module complement_a_2 (
  input  [7:0] in_1,
  output [7:0] out_2
);

  wire [7:0] xor_1_out;

  xor xor_1 (xor_1_out[0], 1'b1, in_1[0]);
  xor xor_2 (xor_1_out[1], 1'b1, in_1[1]);
  xor xor_3 (xor_1_out[2], 1'b1, in_1[2]);
  xor xor_4 (xor_1_out[3], 1'b1, in_1[3]);
  xor xor_5 (xor_1_out[4], 1'b1, in_1[4]);
  xor xor_6 (xor_1_out[5], 1'b1, in_1[5]);
  xor xor_7 (xor_1_out[6], 1'b1, in_1[6]);
  xor xor_8 (xor_1_out[7], 1'b1, in_1[7]);
  Adder adder_1 (.a(8'h1), .b(xor_1_out), .out(out_2));  // open: cin, cout
endmodule
