// Logisim project dlamerde.circ as structural Verilog: 4 circuits, main circuit main
module main (
  input  in_1,
  input  [7:0] in_2,
  input  [7:0] in_3,
  output [7:0] out_4,
  output out_5
);

  BitAdder bitadder_1 ();  // open: in0, out
  Adder adder_1 (.a(in_2), .b(in_3), .out(out_4), .cin(in_1), .cout(out_5));
endmodule

module op (
  input  [7:0] rs,
  input  [7:0] rt,
  input  [7:0] halt,
  input  [2:0] in_4,
  output [3:0] Flags,
  output [7:0] out_6
);

  wire adder_1_cout, and_1_out, and_2_out, and_4_out, and_5_out, and_6_out, and_7_out, and_8_out, and_9_out,
       and_10_out, and_11_out, and_12_out, or_2_out, or_3_out, subtractor_1_bout;
  wire [7:0] adder_1_out, and_3_out, not_1_out, or_1_out, shifter_1_out, shifter_2_out, subtractor_1_out;

  and and_1 (and_1_out, ~rs[7], ~rt[7]);  // AND_Gate
  and and_2 (and_2_out, rs[7], rt[7]);
  Adder adder_1 (.a(rs), .b(rt), .out(adder_1_out), .cout(adder_1_cout));  // open: cin
  Subtractor subtractor_1 (.a(rs), .b(rt), .out(subtractor_1_out), .bout(subtractor_1_bout));  // open: bin
  assign or_1_out = rs | rt;  // OR_Gate or_1, 8 bits wide
  assign and_3_out = rs & rt;  // AND_Gate and_3, 8 bits wide
  assign not_1_out = ~rs;  // NOT_Gate not_1, 8 bits wide
  Shifter shifter_1 (.in(rs), .\dist (rt[2:0]), .out(shifter_1_out));
  Shifter #(.shift("lr")) shifter_2 (.in(rs), .\dist (rt[2:0]), .out(shifter_2_out));
  and and_4 (and_4_out, and_1_out, adder_1_out[7]);
  or or_2 (or_2_out, and_2_out, and_1_out);
  and and_5 (and_5_out, and_2_out, ~adder_1_out[7]);  // AND_Gate
  or or_3 (or_3_out, and_4_out, and_5_out);
  and and_6 (and_6_out, subtractor_1_out[7], or_2_out);
  and and_7 (and_7_out, and_6_out, and_10_out);
  Multiplexer #(.select(3), .width(8)) multiplexer_1 (
    .in0(halt), .in1(adder_1_out), .in2(subtractor_1_out), .in3(or_1_out), .in4(and_3_out), .in5(not_1_out),
    .in6(shifter_1_out), .in7(shifter_2_out), .out({Flags[2], out_6[6:0]}), .sel(in_4));  // open: en
  or or_4 (Flags[3], and_7_out, and_8_out);
  and and_8 (and_8_out, and_9_out, or_3_out);
  nor nor_1 (Flags[1], out_6[0], out_6[1], out_6[2], out_6[3], out_6[4], out_6[5], out_6[6], Flags[2]);
  and and_9 (and_9_out, in_4[0], ~in_4[1], ~in_4[2]);  // AND_Gate
  and and_10 (and_10_out, ~in_4[0], in_4[1], ~in_4[2]);  // AND_Gate
  or or_5 (Flags[0], and_11_out, and_12_out);
  and and_11 (and_11_out, adder_1_cout, and_9_out);
  and and_12 (and_12_out, subtractor_1_bout, and_10_out);

  assign out_6[7] = Flags[2];

  // Notes on the sheet:
  //   OF pour sub
  //   OF pour l'addition
  //   ZF
  //   osef de sa valeur
  //   code add
  //   code sub
  //   OP code add
  //   OF
  //   SF
  //   CF add
  //   Of SF ZF CF
  //   CF sub
endmodule

module a2__unsigned (
  input  [7:0] in_1,
  output [7:0] out_2
);

  wire [7:0] subtractor_1_out, xor_1_out;

  xor xor_1 (xor_1_out[0], 1'b1, in_1[0]);
  xor xor_2 (xor_1_out[1], 1'b1, in_1[1]);
  xor xor_3 (xor_1_out[2], 1'b1, in_1[2]);
  xor xor_4 (xor_1_out[3], 1'b1, in_1[3]);
  xor xor_5 (xor_1_out[4], 1'b1, in_1[4]);
  xor xor_6 (xor_1_out[5], 1'b1, in_1[5]);
  xor xor_7 (xor_1_out[6], 1'b1, in_1[6]);
  xor xor_8 (xor_1_out[7], 1'b1, in_1[7]);
  Subtractor subtractor_1 (.a(xor_1_out), .b(8'h1), .out(subtractor_1_out));  // open: bin, bout
  Multiplexer #(.width(8)) multiplexer_1 (.in0(in_1), .in1(subtractor_1_out), .out(out_2), .sel(in_1[7]));  // open: en
endmodule

module test (
  input  [7:0] rs,
  input  [7:0] rt,
  output [3:0] Flags,
  output [7:0] out_4
);

  wire and_1_out, and_2_out, and_3_out, and_4_out, subtractor_1_bout;

  Subtractor subtractor_1 (.a(rs), .b(rt), .out({Flags[2], out_4[6:0]}), .bout(subtractor_1_bout));  // open: bin
  and and_1 (and_1_out, ~rs[7], ~rt[7]);  // AND_Gate
  and and_2 (and_2_out, rs[7], rt[7]);
  and and_3 (and_3_out, and_1_out, Flags[2]);
  and and_4 (and_4_out, and_2_out, ~Flags[2]);  // AND_Gate
  or or_1 (Flags[3], and_3_out, and_4_out);
  NotExactlyOne xnor_1 (
    .out(Flags[1]), .in0(out_4[0]), .in1(out_4[1]), .in2(out_4[2]), .in3(out_4[3]), .in4(out_4[4]),
    .in5(out_4[5]), .in6(out_4[6]), .in7(Flags[2]));

  assign out_4[7] = Flags[2];

  // Notes on the sheet:
  //   OF pour l'addition
  //   ZF
  //   halt
  //   SF
  //   Of SF ZF CF
endmodule
