// Logisim project massive_octo_computing_machine.circ as structural Verilog: 3 circuits, main circuit main
module main (
  input  [3:0] in_1,
  input  [3:0] in_2,
  output [1:0] out_3,
  output out_4,
  output out_5,
  output out_6,
  output [2:0] out_7
);

  controle_de_saut controle_de_saut_1 (.OF_SF_ZF_CF(in_1), .opcode(in_2), .out_3(out_3));
  decodeur_instruction decodeur_instruction_1 (
    .regWrite(out_5), .out_3(out_4), .isLoad(out_6), .in_1(in_2), .out_4(out_7));
endmodule

module decodeur_instruction (
  input  [3:0] in_1,
  output regWrite,
  output out_3,
  output [2:0] out_4,
  output isLoad
);

  wire and_1_out, not_1_out, not_2_out, or_1_out, or_2_out, or_3_out;
  wire [2:0] and_5_out;

  not not_1 (not_1_out, in_1[3]);
  and and_1 (and_1_out, in_1[1], ~in_1[0]);  // AND_Gate
  not not_2 (not_2_out, in_1[3]);
  or or_1 (or_1_out, in_1[0], in_1[1], in_1[2]);
  or or_2 (or_2_out, not_1_out, isLoad);
  or or_3 (or_3_out, ~in_1[2], ~in_1[1], and_1_out);  // OR_Gate
  and and_2 (regWrite, or_1_out, or_2_out);
  and and_3 (out_3, in_1[3], or_3_out);
  and and_4 (isLoad, in_1[0], in_1[1], in_1[2], in_1[3]);
  and and_5 (and_5_out[0], in_1[0], not_2_out);
  and and_6 (and_5_out[1], in_1[1], not_2_out);
  and and_7 (and_5_out[2], in_1[2], not_2_out);
  Multiplexer #(.width(3)) multiplexer_1 (.in0(and_5_out), .in1(3'b010), .out(out_4), .sel(out_3));  // open: en

  // Notes on the sheet:
  //   abcd
  //   isJump
  //   isUAL
endmodule

module controle_de_saut (
  input  [3:0] OF_SF_ZF_CF,
  input  [3:0] opcode,
  output [1:0] out_3
);

  wire and_1_out, and_2_out, and_3_out, and_4_out, and_5_out, and_6_out, and_7_out, and_8_out, and_9_out,
       and_10_out, and_11_out, and_12_out, and_13_out, and_14_out, and_15_out, and_16_out, B_out, BEQ_out,
       BGE_out, BGT_out, BLE_out, BLT_out, BNE_out, or_1_out, or_2_out, or_3_out, or_4_out, or_5_out;

  and and_1 (and_1_out, ~opcode[3], ~opcode[2], ~opcode[1], ~opcode[0]);  // AND_Gate
  and B (B_out, ~opcode[2], ~opcode[1], ~opcode[0]);  // AND_Gate
  and and_2 (and_2_out, ~opcode[2], ~opcode[1], opcode[0]);  // AND_Gate
  and and_3 (and_3_out, ~opcode[2], opcode[1], ~opcode[0]);  // AND_Gate
  and and_4 (and_4_out, ~opcode[2], opcode[1], opcode[0]);  // AND_Gate
  and and_5 (and_5_out, opcode[2], ~opcode[1], ~opcode[0]);  // AND_Gate
  and and_6 (and_6_out, opcode[2], ~opcode[1], opcode[0], ~OF_SF_ZF_CF[1]);  // AND_Gate
  and and_7 (and_7_out, opcode[2], opcode[1], ~opcode[0], ~OF_SF_ZF_CF[1]);  // AND_Gate
  and BEQ (BEQ_out, OF_SF_ZF_CF[1], and_2_out);
  and BNE (BNE_out, ~OF_SF_ZF_CF[1], and_3_out);  // AND_Gate
  and and_8 (and_8_out, OF_SF_ZF_CF[2], OF_SF_ZF_CF[3]);
  or or_1 (or_1_out, and_8_out, OF_SF_ZF_CF[1], and_9_out);
  and and_9 (and_9_out, ~OF_SF_ZF_CF[3], ~OF_SF_ZF_CF[2]);  // AND_Gate
  and and_10 (and_10_out, ~OF_SF_ZF_CF[3], OF_SF_ZF_CF[2]);  // AND_Gate
  or or_2 (or_2_out, and_10_out, OF_SF_ZF_CF[1], and_11_out);
  and and_11 (and_11_out, OF_SF_ZF_CF[3], ~OF_SF_ZF_CF[2]);  // AND_Gate
  and and_12 (and_12_out, ~OF_SF_ZF_CF[3], ~OF_SF_ZF_CF[2]);  // AND_Gate
  or or_3 (or_3_out, and_12_out, and_13_out);
  and and_13 (and_13_out, OF_SF_ZF_CF[3], OF_SF_ZF_CF[2]);
  and and_14 (and_14_out, ~OF_SF_ZF_CF[2], OF_SF_ZF_CF[3]);  // AND_Gate
  or or_4 (or_4_out, and_14_out, and_15_out);
  and and_15 (and_15_out, OF_SF_ZF_CF[2], ~OF_SF_ZF_CF[3]);  // AND_Gate
  and BGE (BGE_out, or_1_out, and_4_out);
  and BLE (BLE_out, or_2_out, and_5_out);
  and BGT (BGT_out, or_3_out, and_6_out);
  and BLT (BLT_out, or_4_out, and_7_out);
  or or_5 (or_5_out, B_out, BEQ_out, BNE_out, BGE_out, BLE_out, BGT_out, BLT_out);
  and and_16 (and_16_out, or_5_out, opcode[3]);
  not not_1 (out_3[1], and_16_out);
  or or_6 (out_3[0], and_16_out, and_1_out);

  // Notes on the sheet:
  //   ABCD
  //   halt
  //   Saut
endmodule
