// Logisim project massive_octo_computing_machine.circ as structural Verilog: 3 circuits, main circuit main
module main (
  input  [3:0] in_1,
  output out_2,
  output out_3,
  output out_4,
  output [2:0] out_5
);

  decodeur_instruction decodeur_instruction_1 (
    .regWrite(out_3), .isJump(out_2), .isLoad(out_4), .out_5(out_5), .in_1(in_1));
endmodule

module decodeur_instruction (
  input  [3:0] in_1,
  output regWrite,
  output isJump,
  output isLoad,
  output [2:0] out_5
);

  wire and_1_out, not_1_out, not_2_out, or_1_out, or_2_out;

  and and_1 (and_1_out, in_1[1], ~in_1[0]);  // AND_Gate
  not not_1 (not_1_out, in_1[3]);
  or or_1 (or_1_out, in_1[0], in_1[1], in_1[2]);
  not not_2 (not_2_out, in_1[3]);
  or or_2 (or_2_out, ~in_1[2], ~in_1[1], and_1_out);  // OR_Gate
  and and_2 (regWrite, or_1_out, not_2_out);
  and and_3 (isJump, in_1[3], or_2_out);
  and and_4 (isLoad, in_1[0], in_1[1], in_1[2], in_1[3]);
  and and_5 (out_5[0], in_1[0], not_1_out);
  and and_6 (out_5[1], in_1[1], not_1_out);
  and and_7 (out_5[2], in_1[2], not_1_out);

  // Notes on the sheet:
  //   abcd
  //   isUAL
endmodule

module controle_de_saut (
  input  [3:0] CF_ZF_SF_OF,
  input  [3:0] opcode,
  output saut,
  output out_4,
  output out_5,
  output opsuiv,
  output halt
);

  wire and_2_out, and_3_out, or_1_out, or_2_out;

  or or_1 (or_1_out, ~opcode[0], ~opcode[1], ~opcode[2]);  // OR_Gate
  or or_2 (or_2_out, opcode[2], opcode[1], opcode[0]);
  and and_1 (halt, ~opcode[3], ~opcode[2], ~opcode[1], ~opcode[0]);  // AND_Gate
  and and_2 (and_2_out, opcode[3], opcode[2], opcode[1], opcode[0]);
  and and_3 (and_3_out, or_2_out, ~opcode[3]);  // AND_Gate
  or or_3 (opsuiv, and_2_out, and_3_out);
  and and_4 (saut, or_1_out, opcode[3]);
endmodule
